# Fritzing sketch CU-1106-C (saved by Fritzing 0.9.7b)
breadboards: 2

parts:
  CO2_SENSOR = CU-1106 [part_number=CU-1106]
  S1 = Pushbutton [package="[THT]"]
  R2 = Resistor [tolerance=±5% resistance=10k package="0402 [SMD]"]
  MICROCONTROLLER = Arduino Mega 2560 (Rev3)
  0_1_uF = Capacitor [package=cap-pth-small2]

nets:
  N1: CO2_SENSOR.CON5-2, MICROCONTROLLER.D18/TX1
  N2: CO2_SENSOR.CON5-3, MICROCONTROLLER.D19/RX1
  VCC: CO2_SENSOR.CON5-4, CO2_SENSOR.CON4-1, S1.Pin_1, S1.Pin_2, MICROCONTROLLER.5V, 0_1_uF.2
  GND: CO2_SENSOR.CON4-2, R2.Pin_1, MICROCONTROLLER.GND, 0_1_uF.1
  N3: S1.Pin_3, S1.Pin_4, R2.Pin_0, MICROCONTROLLER.D2_PWM

custom parts:
  CU-1106: NDIR CO2 sensor
