# Fritzing sketch CU-1106SL-NS (saved by Fritzing 0.9.7b)
breadboards: 2

parts:
  CO2_SENSOR = CU-1106 [part_number=CU-1106]
  S1 = Pushbutton [package="[THT]"]
  MICROCONTROLLER = Arduino Mega 2560 (Rev3)
  R2 = Resistor [tolerance=±5% resistance=10k package="0402 [SMD]"]

nets (from the breadboard view):
  N1: CO2_SENSOR.CON5-1, MICROCONTROLLER.GND, R2.Pin_1
  N2: CO2_SENSOR.CON5-2, CO2_SENSOR.CON5-3, CO2_SENSOR.CON4-1, S1.Pin_3, S1.Pin_4, MICROCONTROLLER.5V
  N3: CO2_SENSOR.CON5-4, MICROCONTROLLER.D18/TX1
  N4: CO2_SENSOR.CON5-5, MICROCONTROLLER.D19/RX1
  N5: CO2_SENSOR.CON4-3, MICROCONTROLLER.D3_PWM
  N6: S1.Pin_1, S1.Pin_2, MICROCONTROLLER.D2_PWM, R2.Pin_0

custom parts:
  CU-1106: NDIR CO2 sensor
