# Fritzing sketch CU-1106_Part (saved by Fritzing 0.9.7b)
breadboards: 2

parts:
  Part1 = CU-1106 [part_number=CU-1106]
  Part2 = Arduino Uno (Rev3)

nets:
  N1: Part1.CON5-1, Part2.GND
  N2: Part1.CON5-2, Part1.CON4-1, Part2.5V

custom parts:
  CU-1106: NDIR CO2 sensor
