# Fritzing sketch DS3231 (saved by Fritzing 0.9.7b)
breadboards: 1

parts:
  MICROCONTROLLER = Arduino Uno (Rev3)
  RTC_MODULE = ZS-042 RTC Module
  R1 = Resistor [tolerance=±5% resistance=5k package="2010 [SMD]"]
  R2 = Resistor [tolerance=±5% resistance=5k package="2010 [SMD]"]

nets:
  N1: MICROCONTROLLER.A4/SDA, RTC_MODULE.SDA, R2.Pin_0
  N2: MICROCONTROLLER.A5/SCL, RTC_MODULE.SCL, R1.Pin_0
  GND: MICROCONTROLLER.GND, RTC_MODULE.GND
  VCC: MICROCONTROLLER.5V, RTC_MODULE.VCC, R1.Pin_1, R2.Pin_1

notes:
  CSR Modules: DS3231
