# Fritzing sketch DS18B20_Logger_Risky (saved by Fritzing 0.9.7b)
breadboards: 1

parts:
  R4 = Resistor [tolerance=±5% power=0.25 resistance=330 package=THT]
  LED_INDICATOR = smd LED [color="Red (633nm)" package="0805 [SMD]"]
  R6 = Resistor [tolerance=±5% resistance=10k package="0402 [SMD]"]
  R7 = Resistor [tolerance=±5% resistance=10k package="0402 [SMD]"]
  TOGGLE_SWITCH = Toggle Switch [package=THT]
  RTC_MODULE = ZS-042 RTC Module
  C1 = Ceramic Capacitor [capacitance=470nF voltage=50V package="100 mil [THT, multilayer]"]
  C2 = Ceramic Capacitor [capacitance=470nF voltage=35V package="100 mil [THT, multilayer]"]
  Part1 = Arduino Uno (Rev3)
  DS1 = DS18B20 1-Wire Temperature Sensor [part_number=DS18B20]
  SD_MODULE = MicroSD Card Module
  R8 = Resistor [tolerance=±5% power=0.25 resistance=4.7k package=THT]

nets (from the breadboard view):
  N1: R4.Pin_0, Part1.D4
  N2: R4.Pin_1, LED_INDICATOR.anode
  GND: LED_INDICATOR.cathode, R7.Pin_0, RTC_MODULE.GND, C1.0, C2.0, Part1.GND, DS1.GND, SD_MODULE.GND
  VCC: R6.Pin_0, RTC_MODULE.VCC, C1.1, C2.1, Part1.5V, DS1.VDD, SD_MODULE.VCC, R8.Pin_0
  N3: R6.Pin_1, TOGGLE_SWITCH.L2
  N4: R7.Pin_1, TOGGLE_SWITCH.L1
  N5: TOGGLE_SWITCH.COM, Part1.D3_PWM
  N6: RTC_MODULE.SDA, Part1.A4/SDA
  N7: RTC_MODULE.SCL, Part1.A5/SCL
  N8: Part1.D10_PWM/SS, SD_MODULE.CS
  N9: Part1.D11_PWM/MOSI, SD_MODULE.MOSI
  N10: Part1.D12/MISO, SD_MODULE.MISO
  N11: Part1.D13/SCK, SD_MODULE.SCK
  N12: Part1.D2, DS1.DQ, R8.Pin_1
