# Fritzing sketch DS18B20_Logger_Safer (saved by Fritzing 0.9.7b)
breadboards: 1

parts:
  R4 = Resistor [tolerance=±5% power=0.25 resistance=330 package=THT]
  LED_INDICATOR = smd LED [color="Red (633nm)" package="0805 [SMD]"]
  BUTTON = Momentary Switch [package=ksa_sealed_tac_switch]
  R5 = Resistor [tolerance=±5% resistance=10k package="0402 [SMD]"]
  R6 = Resistor [tolerance=±5% resistance=10k package="0402 [SMD]"]
  R7 = Resistor [tolerance=±5% resistance=10k package="0402 [SMD]"]
  TOGGLE_SWITCH = Toggle Switch [package=THT]
  RTC_MODULE = ZS-042 RTC Module
  SD_MODULE = MicroSD Card Module
  C1 = Ceramic Capacitor [capacitance=470nF voltage=50V package="100 mil [THT, multilayer]"]
  C2 = Ceramic Capacitor [capacitance=470nF voltage=35V package="100 mil [THT, multilayer]"]
  LOGIC_CONVERTER = I2C level shifter bidirectional
  Part1 = Arduino Uno (Rev3) - ICSP
  DS1 = DS18B20 1-Wire Temperature Sensor [part_number=DS18B20]

nets:
  LED: R4.Pin_0
  N1: R4.Pin_1, LED_INDICATOR.anode
  GND: LED_INDICATOR.cathode, R5.Pin_0, R7.Pin_0, RTC_MODULE.GND, SD_MODULE.GND, C1.0, C2.0, LOGIC_CONVERTER.GND, DS1.GND
  5V: BUTTON.1, R6.Pin_0, RTC_MODULE.VCC, SD_MODULE.VCC, C1.1, C2.1, LOGIC_CONVERTER.HV, DS1.VDD
  BUTTON: BUTTON.3, R5.Pin_1
  N2: R6.Pin_1, TOGGLE_SWITCH.L2
  N3: R7.Pin_1, TOGGLE_SWITCH.L1
  SWITCH: TOGGLE_SWITCH.COM
  N4: RTC_MODULE.SDA, Part1.A4/SDA
  N5: RTC_MODULE.SCL, Part1.A5/SCL
  MISO: SD_MODULE.MISO
  MOSI 3V: SD_MODULE.MOSI, LOGIC_CONVERTER.LV1
  SCK 3V: SD_MODULE.SCK, LOGIC_CONVERTER.LV2
  CS 3V: SD_MODULE.CS, LOGIC_CONVERTER.LV3
  3.3V: LOGIC_CONVERTER.LV
  MOSI 5V: LOGIC_CONVERTER.HV1
  SCK 5V: LOGIC_CONVERTER.HV2
  CS 5V: LOGIC_CONVERTER.HV3
