# Fritzing sketch CU-1106_Part (saved by Fritzing 0.9.7b)
breadboards: 2

parts:
  Part1 = CU-1106 [part_number=CU-1106]
  Part2 = Arduino Uno (Rev3)
  S1 = Pushbutton [package="[THT]"]
  LED1 = LED - 3mm [color="Red (633nm)" current=0.030 package="3 mm [THT]"]
  R1 = Resistor [tolerance=±5% resistance=220 package="0402 [SMD]"]
  R2 = Resistor [tolerance=±5% resistance=220 package="0402 [SMD]"]
  R3 = Resistor [tolerance=±5% resistance=220 package="0402 [SMD]"]

nets:
  N1: Part1.CON5-1, Part2.GND, R1.Pin_0, R2.Pin_0
  N2: Part1.CON5-2, Part1.CON4-1, Part2.5V, R3.Pin_0
  N3: Part1.CON4-3, LED1.anode
  N4: S1.Pin_1, S1.Pin_2, R2.Pin_1
  N5: S1.Pin_3, S1.Pin_4, R3.Pin_1
  N6: LED1.cathode, R1.Pin_1

custom parts:
  CU-1106: NDIR CO2 sensor
