# Fritzing sketch Davis (saved by Fritzing 0.9.7b)
breadboards: 1

parts:
  CONNECTOR = RJ45 Jack [package=rj45-8]
  MICROCONTROLLER = Arduino Uno (Rev3)
  R1 = Resistor [tolerance=±5% resistance=4.7k package="2010 [SMD]"]

nets:
  5V: CONNECTOR.1, MICROCONTROLLER.5V, R1.Pin_0
  DIRECTION: CONNECTOR.2, MICROCONTROLLER.A3
  GND: CONNECTOR.3, MICROCONTROLLER.GND
  SPEED: CONNECTOR.4, MICROCONTROLLER.D2, R1.Pin_1

custom parts:
  RJ45 Jack: RJ45 Jack Simple RJ45, 8-pin connection - connector for common Cat5, Cat5e, and Cat6 Ethernet cables. Footprint not yet proven in production. Connector sku is PRT-00643; Breakout PCB sku is BOB-00716.
