# Fritzing sketch SDCard_Uno_Safer (saved by Fritzing 0.9.7b)
breadboards: 1

parts:
  SD_CARD_MODULE = MicroSD Card Module
  TOGGLE_SWITCH = Toggle Switch [package=THT]
  R1 = Resistor [tolerance=±5% resistance=10k package="0402 [SMD]"]
  R2 = Resistor [tolerance=±5% resistance=10k package="0402 [SMD]"]
  LOGIC_CONVERTER = I2C level shifter bidirectional
  MICROCONTROLLER = Arduino Uno (Rev3)

nets:
  GND: SD_CARD_MODULE.GND, R2.Pin_0, LOGIC_CONVERTER.GND, MICROCONTROLLER.GND
  5V: SD_CARD_MODULE.VCC, R1.Pin_0, LOGIC_CONVERTER.HV, MICROCONTROLLER.5V
  MISO: SD_CARD_MODULE.MISO, MICROCONTROLLER.D12/MISO
  MOSI 3V: SD_CARD_MODULE.MOSI, LOGIC_CONVERTER.LV2
  SCK 3V: SD_CARD_MODULE.SCK, LOGIC_CONVERTER.LV1
  CS 3V: SD_CARD_MODULE.CS, LOGIC_CONVERTER.LV3
  N1: TOGGLE_SWITCH.L1, R2.Pin_1
  SWITCH: TOGGLE_SWITCH.COM, MICROCONTROLLER.D3_PWM
  N2: TOGGLE_SWITCH.L2, R1.Pin_1
  3.3V: LOGIC_CONVERTER.LV, MICROCONTROLLER.3V3
  SCK 5V: LOGIC_CONVERTER.HV1, MICROCONTROLLER.D13/SCK
  MOSI 5V: LOGIC_CONVERTER.HV2, MICROCONTROLLER.D11_PWM/MOSI
  CS 5V: LOGIC_CONVERTER.HV3, MICROCONTROLLER.D10_PWM/SS
