# Fritzing sketch SDCard_Mega_Risky (saved by Fritzing 0.9.7b)
breadboards: 1

parts:
  SD_CARD_MODULE = MicroSD Card Module
  TOGGLE_SWITCH = Toggle Switch [package=THT]
  R1 = Resistor [tolerance=±5% resistance=10k package="0402 [SMD]"]
  R2 = Resistor [tolerance=±5% resistance=10k package="0402 [SMD]"]
  MICROCONTROLLER = Arduino Mega 2560 (Rev3)

nets:
  GND: SD_CARD_MODULE.GND, R2.Pin_0, MICROCONTROLLER.GND
  5V: SD_CARD_MODULE.VCC, R1.Pin_0, MICROCONTROLLER.5V
  N1: SD_CARD_MODULE.MISO, MICROCONTROLLER.D50
  N2: SD_CARD_MODULE.MOSI, MICROCONTROLLER.D51
  N3: SD_CARD_MODULE.SCK, MICROCONTROLLER.D52
  N4: SD_CARD_MODULE.CS, MICROCONTROLLER.D53
  N5: TOGGLE_SWITCH.L1, R2.Pin_1
  N6: TOGGLE_SWITCH.COM, MICROCONTROLLER.D3_PWM
  N7: TOGGLE_SWITCH.L2, R1.Pin_1
