# Fritzing sketch SDCard_Mega_Safer (saved by Fritzing 0.9.7b)
breadboards: 1

parts:
  SD_CARD_MODULE = MicroSD Card Module
  TOGGLE_SWITCH = Toggle Switch [package=THT]
  R1 = Resistor [tolerance=±5% resistance=10k package="0402 [SMD]"]
  R2 = Resistor [tolerance=±5% resistance=10k package="0402 [SMD]"]
  MICROCONTROLLER = Arduino Mega 2560 (Rev3)
  LOGIC_CONVERTER = I2C level shifter bidirectional

nets:
  GND: SD_CARD_MODULE.GND, R2.Pin_0, MICROCONTROLLER.GND, LOGIC_CONVERTER.GND
  5V: SD_CARD_MODULE.VCC, R1.Pin_0, MICROCONTROLLER.5V, LOGIC_CONVERTER.HV
  MISO: SD_CARD_MODULE.MISO, MICROCONTROLLER.D50
  MOSI 3V: SD_CARD_MODULE.MOSI, LOGIC_CONVERTER.LV2
  SCK 3V: SD_CARD_MODULE.SCK, LOGIC_CONVERTER.LV1
  CS 3V: SD_CARD_MODULE.CS, LOGIC_CONVERTER.LV3
  N1: TOGGLE_SWITCH.L1, R2.Pin_1
  SWITCH: TOGGLE_SWITCH.COM, MICROCONTROLLER.D3_PWM
  N2: TOGGLE_SWITCH.L2, R1.Pin_1
  3.3V: MICROCONTROLLER.3V3, LOGIC_CONVERTER.LV
  MOSI 5V: MICROCONTROLLER.D51, LOGIC_CONVERTER.HV2
  SCK 5V: MICROCONTROLLER.D52, LOGIC_CONVERTER.HV1
  CS 5V: MICROCONTROLLER.D53, LOGIC_CONVERTER.HV3
