# Fritzing sketch MH-Z16_I2C_Schematic (saved by Fritzing 0.9.7b)

parts:
  I2C_ADAPTOR_FOR_MH-Z16 = Grove 3 Axis Digital Accelerometer 16g
  MICROCONTROLLER = Arduino Uno (Rev3)

nets:
  GND: I2C_ADAPTOR_FOR_MH-Z16.GND, MICROCONTROLLER.GND
  VCC: I2C_ADAPTOR_FOR_MH-Z16.VCC, MICROCONTROLLER.5V
  N1: I2C_ADAPTOR_FOR_MH-Z16.SDA, MICROCONTROLLER.A4/SDA
  N2: I2C_ADAPTOR_FOR_MH-Z16.SCL, MICROCONTROLLER.A5/SCL

notes:
  CSR Modules: MH-Z16 w/ I2C
