# Fritzing sketch MultiRTC (saved by Fritzing 0.9.7b)
breadboards: 1

parts:
  MICROCONTROLLER = Arduino Nano (Rev3.0)
  I2C_MULTIPLEXER = Adafruit TCA9548A
  RTC#3 = ZS-042 RTC Module
  RTC#0 = ZS-042 RTC Module
  RTC#1 = ZS-042 RTC Module
  RTC#2 = ZS-042 RTC Module
  R1 = Resistor [tolerance=±5% power=0.25 resistance=5k package=THT]
  R2 = Resistor [tolerance=±5% power=0.25 resistance=5k package=THT]

nets:
  GND: MICROCONTROLLER.GND, I2C_MULTIPLEXER.GND, RTC#3.GND, RTC#0.GND, RTC#1.GND, RTC#2.GND
  5V: MICROCONTROLLER.5V, I2C_MULTIPLEXER.VCC, RTC#3.VCC, RTC#0.VCC, RTC#1.VCC, RTC#2.VCC, R1.Pin_1, R2.Pin_1
  SCL_5V: MICROCONTROLLER.A5, I2C_MULTIPLEXER.INPUTSCL, R2.Pin_0
  SDA_5V: MICROCONTROLLER.A4, I2C_MULTIPLEXER.INPUTSDA, R1.Pin_0
  SDA#2: I2C_MULTIPLEXER.2SDA, RTC#2.SDA
  SCL#2: I2C_MULTIPLEXER.2SCL, RTC#2.SCL
  SDA#3: I2C_MULTIPLEXER.3SDA, RTC#3.SDA
  SCL#3: I2C_MULTIPLEXER.3SCL, RTC#3.SCL
  SDA#0: I2C_MULTIPLEXER.0SDA, RTC#0.SDA
  SCL#0: I2C_MULTIPLEXER.0SCL, RTC#0.SCL
  SDA#1: I2C_MULTIPLEXER.1SDA, RTC#1.SDA
  SCL#1: I2C_MULTIPLEXER.1SCL, RTC#1.SCL

custom parts:
  Adafruit TCA9548A: You just found the perfect I2C sensor, and you want to wire up two or three or more of them to your Arduino when you realize "Uh oh, this chip has a fixed I2C address, and from what I know about I2C, you cannot have two devices with the same address on the same SDA/SCL pins!" Are you out of luck? You would be, if you didn't have this ultra-cool TCA9548A 1-to-8 I2C multiplexer! Finally, a way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
