# Fritzing sketch SCD30_5V (saved by Fritzing 0.9.7b)
breadboards: 1

parts:
  CO2_SENSOR = SCD30
  MICROCONTROLLER = Arduino Uno (Rev3) - ICSP

nets:
  VDD: CO2_SENSOR.VDD, MICROCONTROLLER.5V
  GND: CO2_SENSOR.GND, MICROCONTROLLER.GND
  N1: CO2_SENSOR.TX/SCL, MICROCONTROLLER.A5/SCL
  N2: CO2_SENSOR.RX/SDA, MICROCONTROLLER.A4/SDA

notes:
  CSR Modules: SCD30 at 5V

custom parts:
  SCD30: CO2 , humidity, and temperature sensor * Current consumption: 19 mA @ 1 meas. per 2 s. * Digital interface UART or I2C * Company: Sensirion - The Sensor Company Electrical specifications * average current: 19 mA * max. current: 75 mA * DC supply: 3.3 V - 5.5 V Operation conditions * temperature: 0 – 50°C * humidity: 0 – 95 %RH * sensor lifetime: 15 years CO2-sensor: * NDIR CO 2 sensor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
