# Fritzing sketch SCD30_Circuit_3V (saved by Fritzing 0.9.7b)
breadboards: 1

parts:
  Part1 = SCD30  # not connected
  Part2 = I2C level shifter bidirectional
  Part3 = Arduino Ethernet Shield (Rev3)

nets:
  GND: Part2.GND, Part3.GND
  N1: Part2.LV, Part3.3V3
  N2: Part2.HV1, Part3.A4/SDA
  N3: Part2.HV2, Part3.A5/SCL
  N4: Part2.HV, Part3.5V

custom parts:
  SCD30: CO2 , humidity, and temperature sensor * Current consumption: 19 mA @ 1 meas. per 2 s. * Digital interface UART or I2C * Company: Sensirion - The Sensor Company Electrical specifications * average current: 19 mA * max. current: 75 mA * DC supply: 3.3 V - 5.5 V Operation conditions * temperature: 0 – 50°C * humidity: 0 – 95 %RH * sensor lifetime: 15 years CO2-sensor: * NDIR CO 2 sensor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
