# Fritzing sketch SCD30_Circuit_3V (saved by Fritzing 0.9.7b)
breadboards: 1

parts:
  CO2_SENSOR = SCD30
  I2C_LEVEL_CONVERTER = I2C level shifter bidirectional
  MICROCONTROLLER = Arduino Uno (Rev3)

nets:
  5V: CO2_SENSOR.VDD, I2C_LEVEL_CONVERTER.HV, MICROCONTROLLER.5V
  GND: CO2_SENSOR.GND, I2C_LEVEL_CONVERTER.GND, MICROCONTROLLER.GND
  SCL 3.3V: CO2_SENSOR.TX/SCL, I2C_LEVEL_CONVERTER.LV2
  SDA 3.3V: CO2_SENSOR.RX/SDA, I2C_LEVEL_CONVERTER.LV1
  3.3V: I2C_LEVEL_CONVERTER.LV, MICROCONTROLLER.3V3
  SDA 5V: I2C_LEVEL_CONVERTER.HV1, MICROCONTROLLER.A4/SDA
  SCL 5V: I2C_LEVEL_CONVERTER.HV2, MICROCONTROLLER.A5/SCL

notes:
  CSR Modules: SCD-30 at 3.3V

custom parts:
  SCD30: CO2 , humidity, and temperature sensor * Current consumption: 19 mA @ 1 meas. per 2 s. * Digital interface UART or I2C * Company: Sensirion - The Sensor Company Electrical specifications * average current: 19 mA * max. current: 75 mA * DC supply: 3.3 V - 5.5 V Operation conditions * temperature: 0 – 50°C * humidity: 0 – 95 %RH * sensor lifetime: 15 years CO2-sensor: * NDIR CO 2 sensor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
