# Fritzing sketch CU-1106H-NS_LoggerOLD (saved by Fritzing 0.9.7b)
breadboards: 1

parts:
  CO2_SENSOR = CU-1106 [part_number=CU-1106]
  S1 = Pushbutton [package="[THT]"]
  0_1_uF = Capacitor [package=cap-pth-small2]  # not connected
  LED2 = smd LED [color="Red (633nm)" package="0603 [SMD]"]
  Part1 = Arduino Mega ADK (Rev3)
  ZS-042_RTC1 = ZS-042 RTC Module
  microSD1 = MicroSD Card Module
  R5 = Resistor [tolerance=±5% resistance=10k package="0402 [SMD]"]
  R6 = Resistor [tolerance=±5% resistance=330 package="0402 [SMD]"]
  S2 = Toggle Switch [package=THT]  # not connected

nets:
  N1: CO2_SENSOR.CON5-2, Part1.D18/TX1
  N2: CO2_SENSOR.CON5-3, Part1.D19/RX1
  VCC: CO2_SENSOR.CON4-1
  GND: CO2_SENSOR.CON4-2
  N3: S1.Pin_1, S1.Pin_2, Part1.D2_PWM, R5.Pin_0
  5V: S1.Pin_3, S1.Pin_4, Part1.5V, ZS-042_RTC1.VCC
  N4: LED2.cathode, R6.Pin_0
  N5: LED2.anode, Part1.D4_PWM
  N6: Part1.D13_PWM, microSD1.SCK
  N7: Part1.D12_PWM, microSD1.MOSI
  N8: Part1.D11_PWM, microSD1.MISO
  N9: Part1.D10_PWM, microSD1.CS
  GND_2: Part1.GND, ZS-042_RTC1.GND, R5.Pin_1, R6.Pin_1

custom parts:
  CU-1106: NDIR CO2 sensor
