# Fritzing sketch CU-1106H-NS_Logger_Safer (saved by Fritzing 0.9.7b)
breadboards: 1

parts:
  R4 = Resistor [tolerance=±5% power=0.25 resistance=330 package=THT]
  LED_INDICATOR = smd LED [color="Red (633nm)" package="0805 [SMD]"]
  MICROCONTROLLER = Arduino Mega 2560 (Rev3)
  BUTTON = Momentary Switch [package=ksa_sealed_tac_switch]
  R5 = Resistor [tolerance=±5% resistance=10k package="0402 [SMD]"]
  R6 = Resistor [tolerance=±5% resistance=10k package="0402 [SMD]"]
  R7 = Resistor [tolerance=±5% resistance=10k package="0402 [SMD]"]
  TOGGLE_SWITCH = Toggle Switch [package=THT]
  RTC_MODULE = ZS-042 RTC Module
  SD_MODULE = MicroSD Card Module
  CU-1106H-NS = CU-1106 [part_number=CU-1106]
  0_1_uF = Capacitor [package=cap-pth-small2]
  C1 = Ceramic Capacitor [capacitance=470nF voltage=50V package="100 mil [THT, multilayer]"]
  C2 = Ceramic Capacitor [capacitance=470nF voltage=35V package="100 mil [THT, multilayer]"]
  LOGIC_CONVERTER = I2C level shifter bidirectional

nets (from the breadboard view):
  N1: R4.Pin_0, MICROCONTROLLER.D4_PWM
  N2: R4.Pin_1, LED_INDICATOR.anode
  GND: LED_INDICATOR.cathode, MICROCONTROLLER.GND, R5.Pin_0, R7.Pin_0, RTC_MODULE.GND, SD_MODULE.GND, CU-1106H-NS.CON4-2, 0_1_uF.1, C1.0, C2.0, LOGIC_CONVERTER.GND
  N3: MICROCONTROLLER.D21/SCL, MICROCONTROLLER.SCL, RTC_MODULE.SCL
  N4: MICROCONTROLLER.D20/SDA, RTC_MODULE.SDA
  N5: MICROCONTROLLER.D19/RX1, CU-1106H-NS.CON5-3, CU-1106H-NS.CON5-5
  N6: MICROCONTROLLER.D18/TX1, CU-1106H-NS.CON5-2
  N7: MICROCONTROLLER.3V3, LOGIC_CONVERTER.LV
  VCC: MICROCONTROLLER.5V, BUTTON.1, R6.Pin_0, RTC_MODULE.VCC, SD_MODULE.VCC, CU-1106H-NS.CON4-1, 0_1_uF.2, C1.1, C2.1, LOGIC_CONVERTER.HV
  N8: MICROCONTROLLER.D2_PWM, BUTTON.3, R5.Pin_1
  N9: MICROCONTROLLER.D3_PWM, TOGGLE_SWITCH.COM
  N10: MICROCONTROLLER.D50, SD_MODULE.MISO
  N11: MICROCONTROLLER.D51, LOGIC_CONVERTER.HV1
  N12: MICROCONTROLLER.D52, LOGIC_CONVERTER.HV2
  N13: MICROCONTROLLER.D53, LOGIC_CONVERTER.HV3
  N14: R6.Pin_1, TOGGLE_SWITCH.L2
  N15: R7.Pin_1, TOGGLE_SWITCH.L1
  N16: SD_MODULE.MOSI, LOGIC_CONVERTER.LV1
  N17: SD_MODULE.SCK, LOGIC_CONVERTER.LV2
  N18: SD_MODULE.CS, LOGIC_CONVERTER.LV3

notes:
  Although the circuit says MH-Z19, this module is supposed to represent the CU-1106

custom parts:
  CU-1106: NDIR CO2 sensor
