# Fritzing sketch QuadrupleCU-1106_Logger (saved by Fritzing 0.9.7b)
breadboards: 1

parts:
  R4 = Resistor [tolerance=±5% power=0.25 resistance=330 package=THT]
  LED_INDICATOR = smd LED [color="Red (633nm)" package="0805 [SMD]"]
  MICROCONTROLLER = Arduino Mega 2560 (Rev3)
  BUTTON = Momentary Switch [package=ksa_sealed_tac_switch]
  R5 = Resistor [tolerance=±5% resistance=10k package="0402 [SMD]"]
  R6 = Resistor [tolerance=±5% resistance=10k package="0402 [SMD]"]
  R7 = Resistor [tolerance=±5% resistance=10k package="0402 [SMD]"]
  TOGGLE_SWITCH = Toggle Switch [package=THT]
  RTC_MODULE = ZS-042 RTC Module
  SD_MODULE = MicroSD Card Module
  CU-1106H-NS = CU-1106 [part_number=CU-1106]
  0_1_uF = Capacitor [package=cap-pth-small2]
  C1 = Ceramic Capacitor [capacitance=470nF voltage=50V package="100 mil [THT, multilayer]"]
  C2 = Ceramic Capacitor [capacitance=470nF voltage=35V package="100 mil [THT, multilayer]"]
  LOGIC_CONVERTER = I2C level shifter bidirectional
  CU-1106SL-N = CU-1106 [part_number=CU-1106]
  CU-1106SL-NS = CU-1106 [part_number=CU-1106]
  CU-1106SL-C = CU-1106 [part_number=CU-1106]
  U1 = LCD-16X2 [package=lcd-16x2_noholes]

nets (from the breadboard view):
  N1: R4.Pin_0, MICROCONTROLLER.D4_PWM
  N2: R4.Pin_1, LED_INDICATOR.anode
  GND: LED_INDICATOR.cathode, MICROCONTROLLER.GND, R5.Pin_0, R7.Pin_0, RTC_MODULE.GND, SD_MODULE.GND, CU-1106H-NS.CON4-2, 0_1_uF.1, C1.0, C2.0, LOGIC_CONVERTER.GND, CU-1106SL-N.CON5-1, CU-1106SL-NS.CON5-1, CU-1106SL-C.CON4-2, U1.VSS
  N3: MICROCONTROLLER.D21/SCL, MICROCONTROLLER.SCL, RTC_MODULE.SCL, U1.RS
  N4: MICROCONTROLLER.D20/SDA, RTC_MODULE.SDA, U1.VO
  N5: MICROCONTROLLER.D19/RX1, CU-1106H-NS.CON5-3, CU-1106H-NS.CON5-5
  N6: MICROCONTROLLER.D18/TX1, CU-1106H-NS.CON5-1, CU-1106H-NS.CON5-2
  N7: MICROCONTROLLER.D17_PWM/RX2, CU-1106SL-N.CON5-5
  N8: MICROCONTROLLER.D16_PWM/TX2, CU-1106SL-N.CON5-4
  N9: MICROCONTROLLER.D15/RX3, CU-1106SL-NS.CON5-5
  N10: MICROCONTROLLER.D14/TX3, CU-1106SL-NS.CON5-4
  N11: MICROCONTROLLER.3V3, LOGIC_CONVERTER.LV
  VCC: MICROCONTROLLER.5V, BUTTON.1, R6.Pin_0, RTC_MODULE.VCC, SD_MODULE.VCC, CU-1106H-NS.CON4-1, 0_1_uF.2, C1.1, C2.1, LOGIC_CONVERTER.HV, CU-1106SL-N.CON5-2, CU-1106SL-N.CON4-1, CU-1106SL-NS.CON5-2, CU-1106SL-NS.CON5-3, CU-1106SL-NS.CON4-1, CU-1106SL-NS.CON4-4, CU-1106SL-C.CON5-4, CU-1106SL-C.CON4-1, U1.VDD
  N12: MICROCONTROLLER.D0_RX0, CU-1106SL-C.CON5-3
  N13: MICROCONTROLLER.D1_TX0, CU-1106SL-C.CON5-2
  N14: MICROCONTROLLER.D2_PWM, BUTTON.3, R5.Pin_1
  N15: MICROCONTROLLER.D3_PWM, TOGGLE_SWITCH.COM
  N16: MICROCONTROLLER.D6_PWM, CU-1106SL-NS.CON4-3
  N17: MICROCONTROLLER.D7_PWM, CU-1106SL-N.CON4-3
  N18: MICROCONTROLLER.D50, SD_MODULE.MISO
  N19: MICROCONTROLLER.D51, LOGIC_CONVERTER.HV1
  N20: MICROCONTROLLER.D52, LOGIC_CONVERTER.HV2
  N21: MICROCONTROLLER.D53, LOGIC_CONVERTER.HV3
  N22: R6.Pin_1, TOGGLE_SWITCH.L2
  N23: R7.Pin_1, TOGGLE_SWITCH.L1
  N24: SD_MODULE.MOSI, LOGIC_CONVERTER.LV1
  N25: SD_MODULE.SCK, LOGIC_CONVERTER.LV2
  N26: SD_MODULE.CS, LOGIC_CONVERTER.LV3

notes:
  Although the circuit says MH-Z19, this module is supposed to represent the CU-1106

custom parts:
  CU-1106: NDIR CO2 sensor
