# Fritzing sketch CU-1106-C_I2C (saved by Fritzing 0.9.7b)
breadboards: 2

parts:
  CO2_SENSOR = CU-1106 [part_number=CU-1106]
  S1 = Pushbutton [package="[THT]"]
  0_1_uF = Capacitor [package=cap-pth-small2]
  Part1 = Arduino Uno (Rev3)
  R2 = Resistor [tolerance=±5% resistance=10k package="0402 [SMD]"]

nets:
  N1: CO2_SENSOR.CON5-2, Part1.A4/SDA
  N2: CO2_SENSOR.CON5-3, Part1.A5/SCL
  GND: CO2_SENSOR.CON5-4, CO2_SENSOR.CON4-2, 0_1_uF.1, Part1.GND, R2.Pin_1
  VCC: CO2_SENSOR.CON4-1, S1.Pin_1, S1.Pin_2, 0_1_uF.2, Part1.5V
  N3: S1.Pin_3, S1.Pin_4, Part1.D2, R2.Pin_0

custom parts:
  CU-1106: NDIR CO2 sensor
